# Fritzing sketch electrical_scheme (saved by Fritzing 0.9.3b)
circuit board: 8.46667cm x 5.64444cm
breadboards: 1

parts:
  Raspberry_Pi2 = Raspberry Pi B rev2
  Part3 = Soil Moisture Sensor
  Part4 = Soil Moisture Sensor
  LED5 = LED - 5mm [color="Green (565nm)" package="5 mm [THT]"]
  LED7 = LED - 5mm [color="Red (633nm)" package="5 mm [THT]"]
  WeMos_D1_Mini_Relay_Shield1 = WeMos D1 Mini Relay Shield
  BAT3 = BC9VPC [package=bc9vpc]
  R7 = Resistor [tolerance=±5% resistance=680 package=THT]
  S6 = Taiway 100-SP-X-T1 SPDT Miniature Toggle Switch [part_number=100-SP-X-T1-0-0-B1-M2 package=THT]
  M2 = DC Motor [part_number=Pompa]
  R11 = Resistor [tolerance=±5% resistance=680 package=THT]
  R15 = Resistor [tolerance=±5% resistance=680 package=THT]
  LED6 = LED - 5mm [color="Yellow (592nm)" package="5 mm [THT]"]
  WeMos_D1_Mini_Relay_Shield2 = WeMos D1 Mini Relay Shield
  T1 = TMP36 Temperature Sensor [package="TO92 [THT]"]

nets (from the breadboard view):
  VCC: Raspberry_Pi2.3V3, Part3.VCC, Part4.VCC, R7.Pin_1, T1.+Vs
  3V3: Raspberry_Pi2.5V, WeMos_D1_Mini_Relay_Shield1.3V3, WeMos_D1_Mini_Relay_Shield2.3V3
  GND: Raspberry_Pi2.GND, Part3.GND, Part4.GND, LED5.cathode, LED7.cathode, WeMos_D1_Mini_Relay_Shield1.RST, S6.COM, LED6.cathode, WeMos_D1_Mini_Relay_Shield2.RST, T1.GND
  N1: Raspberry_Pi2.GPIO_23, R11.Pin_0
  N2: Raspberry_Pi2.GPIO_17, S6.L1
  N3: Raspberry_Pi2.GPIO_18, Part4.SIG
  N4: Raspberry_Pi2.GPIO_27, WeMos_D1_Mini_Relay_Shield2.D7
  N5: Raspberry_Pi2.GPIO_22, R15.Pin_0
  N6: Raspberry_Pi2.GPIO_4, WeMos_D1_Mini_Relay_Shield1.D7
  N7: Raspberry_Pi2.GPIO_24, Part3.SIG
  N8: Raspberry_Pi2.GPIO_25, T1.Vout
  N9: LED5.anode, R15.Pin_1
  N10: LED7.anode, R7.Pin_0
  N11: WeMos_D1_Mini_Relay_Shield1.COM, BAT3.V+, WeMos_D1_Mini_Relay_Shield2.COM
  N12: WeMos_D1_Mini_Relay_Shield1.NO, M2.pin_1, WeMos_D1_Mini_Relay_Shield2.NO
  N13: BAT3.V-, M2.pin_2
  N14: R11.Pin_1, LED6.anode
